# Fritzing sketch DC - DC Elevador (saved by Fritzing 0.9.0b)
breadboards: 1

parts:
  OptoA = Optocoupler [package=THT]
  R1 = Resistor [tolerance=±5% resistance=220 package=THT]
  Batt = Screw terminal - 2 pins [package=THT]
  U1 = 555 Timer [package="DIP8 [THT]"]
  C1 = Electrolytic Capacitor [capacitance=10µF voltage=16V package="100 mil [THT, electrolytic]"]
  C2 = Electrolytic Capacitor [capacitance=100µF voltage=16V package="100 mil [THT, electrolytic]"]
  RT2 = Resistor [tolerance=±5% resistance=10k package=THT]
  CT3 = Ceramic Capacitor [capacitance=3.3nF voltage=35V package="100 mil [THT, multilayer]"]
  ZVP2106A = MOSFET-NCHANNEL [package=to-92]
  RT8 = Resistor [tolerance=±5% resistance=2k package=THT]
  L1 = Inductor [package="400 mil [THT]"]
  L2 = Inductor [package="400 mil [THT]"]
  C5 = Ceramic Capacitor [capacitance=2.2µF voltage=250V package="200 mil [THT, multilayer]"]
  IRF450 = mystery part, 3 pins [chip_label=?]
  RE1 = Resistor [tolerance=±5% resistance=10M package=THT]
  RE2 = Resistor [tolerance=±5% resistance=200k package=THT]
  RT1 = Resistor [tolerance=±5% resistance=20k package=THT]
  R8 = Resistor [tolerance=±5% resistance=100k package=THT]
  BYW95C = Screw terminal - 2 pins [package=THT]
  D1 = Rectifier Diode [part_number=1N4001 package="300 mil [THT]"]
  OptoB = Optocoupler [package=THT]
  Solenoide = Screw terminal - 2 pins [package=THT]
  ROB1 = Resistor [tolerance=±5% resistance=220 package=THT]
  ROB2 = Resistor [tolerance=±5% resistance=100k package=THT]
  IGBT = Screw terminal - 3 pins [package=THT]
  bCapacitores = Screw terminal - 2 pins [package=THT]
  J2 = screw terminal, 3 pins

nets:
  N1: OptoA.Pin_1, R1.Pin_0
  GND_1: OptoA.Pin_2, OptoA.Pin_3, OptoB.Pin_2, J2.pin2
  S_IN: OptoA.Pin_5, U1.Reset, R8.Pin_1
  N2: R1.Pin_1, J2.pin3
  GND: Batt.pin1, U1.Ground, C1.-, C2.-, CT3.0, ZVP2106A.S, C5.0, IRF450.pin1, RE2.Pin_1, OptoB.Pin_4, IGBT.Emisor, bCapacitores.-
  12V/Vbatt: Batt.pin2, U1.Vcc_Supply_Voltage, C1.+, C2.+, RT8.Pin_0, L2.pin_1, RT1.Pin_0, R8.Pin_0, ROB2.Pin_0
  N3: U1.Trigger, U1.Threshold, RT2.Pin_1, CT3.1
  N4: U1.Output, IRF450.pin3
  N5: U1.Control_Voltage, ZVP2106A.D, RT8.Pin_1
  N6: U1.Discharge, RT2.Pin_0, RT1.Pin_1
  Vref: ZVP2106A.G, RE1.Pin_1, RE2.Pin_0
  N7: L1.pin_0, IRF450.pin2, BYW95C.Anodo
  N8: L1.pin_1, L2.pin_0
  N9: C5.1, RE1.Pin_0, BYW95C.Catodo, D1.cathode, Solenoide.pin1, bCapacitores.+
  N10: D1.anode, Solenoide.pin2, IGBT.Colector
  N11: OptoB.Pin_1, ROB1.Pin_0
  N12: OptoB.Pin_5, ROB2.Pin_1, IGBT.Gate
  Disparo: ROB1.Pin_1, J2.pin1

notes:
  DC - DC Elevador, Disparador Futbot 1.0v

custom parts:
  Screw terminal - 2 pins: Screw terminal with 2 pins
  Screw terminal - 3 pins: Screw terminal with 3 pins
  Screw terminal - 2 pins: Screw terminal with 2 pins
