# Fritzing sketch DC - DC Elevadorv2 (saved by Fritzing 0.9.0b)
circuit board: 10cm x 8.53cm
breadboards: 1

parts:
  OptoA = Optocoupler [package=THT]
  ROA1 = Resistor [tolerance=±5% resistance=220 package=THT]
  U1 = 555 Timer [package="DIP8 [THT]"]
  C1 = Electrolytic Capacitor [capacitance=10µF voltage=16V package="100 mil [THT, electrolytic]"]
  CB = Electrolytic Capacitor [capacitance=100µF voltage=16V package="100 mil [THT, electrolytic]"]
  RT2 = Resistor [tolerance=±5% resistance=10k package=THT]
  CT3 = Ceramic Capacitor [capacitance=3.3nF voltage=35V package="100 mil [THT, multilayer]"]
  ZVP2106A = MOSFET-NCHANNEL [package=to-92]
  RT8 = Resistor [tolerance=±5% resistance=2k package=THT]
  L1 = Inductor [package="400 mil [THT]"]
  L2 = Inductor [package="400 mil [THT]"]
  C5 = Ceramic Capacitor [capacitance=2.2µF voltage=250V package="200 mil [THT, multilayer]"]
  IRF450 = mystery part, 3 pins [chip_label=?]
  RE1 = Resistor [tolerance=±5% resistance=10M package=THT]
  RE2 = Resistor [tolerance=±5% resistance=200k package=THT]
  RT1 = Resistor [tolerance=±5% resistance=20k power=500mW package=THT]
  ROA2 = Resistor [tolerance=±5% resistance=100k package=THT]
  BYW95C = Screw terminal - 2 pins [package=THT]
  D1 = Rectifier Diode [part_number=1N4001 package="300 mil [THT]"]
  OptoB = Optocoupler [package=THT]
  Solenoide = Screw terminal - 2 pins [package=THT]
  ROB1 = Resistor [tolerance=±5% resistance=100 package=THT]
  ROB2 = Resistor [tolerance=±5% resistance=100k package=THT]
  bCapacitores = Screw terminal - 2 pins [package=THT]
  Entrada = screw terminal, 3 pins
  rDescarga = Resistor [tolerance=±5% resistance=10k power=10W package=THT]
  S1 = SPST Switch [package=switch-spdt]
  Conectores = female pin header, 2 pins [form="♀ (female)"]
  Batt1 = Screw terminal - 2 pins [package=THT]
  dProteccion1 = Diode [package=diode-1n4001]
  PROTECCIONIGBT = Rectifier Diode [part_number=1N4001 package="300 mil [THT]"]
  IGBT = Screw terminal - 3 pins [package=THT]

nets:
  N1: OptoA.Pin_1, ROA1.Pin_0
  GND_1: OptoA.Pin_2, OptoB.Pin_2, Entrada.pin2
  GND: OptoA.Pin_4, U1.Ground, C1.-, CB.-, CT3.0, ZVP2106A.S, C5.0, IRF450.pin1, RE2.Pin_1, OptoB.Pin_4, bCapacitores.-, rDescarga.Pin_1, Conectores.pin2, Batt1.pin2, PROTECCIONIGBT.anode, IGBT.SOURCE
  S_IN: OptoA.Pin_5, U1.Reset, ROA2.Pin_1
  N2: ROA1.Pin_1, Entrada.pin3
  N3: U1.Trigger, U1.Threshold, RT2.Pin_1, CT3.1
  N4: U1.Output, IRF450.pin3
  N5: U1.Control_Voltage, ZVP2106A.D, RT8.Pin_1
  N6: U1.Discharge, RT2.Pin_0, RT1.Pin_1
  Vbatt: U1.Vcc_Supply_Voltage, C1.+, CB.+, RT8.Pin_0, L2.pin_1, RT1.Pin_0, ROA2.Pin_0, ROB2.Pin_0, dProteccion1.C
  Vref: ZVP2106A.G, RE1.Pin_1, RE2.Pin_0, Conectores.pin1
  N7: L1.pin_0, IRF450.pin2, BYW95C.Anodo
  N8: L1.pin_1, L2.pin_0
  N9: C5.1, RE1.Pin_0, BYW95C.Catodo, D1.cathode, Solenoide.pin1, bCapacitores.+, S1.P
  N10: D1.anode, OptoB.Pin_5, Solenoide.pin2, ROB2.Pin_1, IGBT.GATE
  N11: OptoB.Pin_1, ROB1.Pin_0
  Disparo: ROB1.Pin_1, Entrada.pin1
  N12: rDescarga.Pin_0, S1.O
  N13: Batt1.pin1, dProteccion1.A
  N14: PROTECCIONIGBT.cathode, IGBT.DRAIN

notes:
  DC - DC Elevador, Disparador Futbot 1.0v
  Disparador v1.0

custom parts:
  Screw terminal - 2 pins: Screw terminal with 2 pins
  Screw terminal - 2 pins: Screw terminal with 2 pins
  Screw terminal - 3 pins: Screw terminal with 3 pins
